# Fritzing sketch WorkTimeLoggerSchematic V2 (saved by Fritzing 0.9.3b)
breadboards: 1

parts:
  Part1 = Arduino Uno (Rev3)
  IC1 = IC, SIP package, 8 pins [chip_label=RC522]
  HD44780 = IC, SIP package, 4 pins [chip_label=PCF8574]
  OK = Pushbutton [package="[THT]"]
  ANULUJ = Pushbutton [package="[THT]"]
  R1 = Resistor [tolerance=±5% resistance=4.7k package=THT]
  R2 = Resistor [tolerance=±5% resistance=4.7k package=THT]
  IC2 = IC, DIP package, 12 pins [chip_label=LLC]

nets:
  N1: Part1.A4/SDA, HD44780.pin2
  N2: Part1.A5/SCL, HD44780.pin1
  N3: Part1.D8, OK.Pin_3, OK.Pin_4, R2.Pin_1
  N4: Part1.D9_PWM, IC2.pin6
  N5: Part1.D10_PWM/SS, IC2.pin1
  N6: Part1.D11_PWM/MOSI, IC2.pin5
  N7: Part1.D12/MISO, IC1.pin4
  N8: Part1.D13/SCK, IC2.pin2
  N9: Part1.D2, IC1.pin5
  N10: Part1.D7, ANULUJ.Pin_3, ANULUJ.Pin_4, R1.Pin_1
  N11: Part1.3V3, IC1.pin8, IC2.pin9
  N12: Part1.5V, HD44780.pin3, R1.Pin_0, R2.Pin_0, IC2.pin4
  N13: Part1.GND, HD44780.pin4, OK.Pin_1, OK.Pin_2, ANULUJ.Pin_1, ANULUJ.Pin_2, IC2.pin3
  N14: IC1.pin1, IC2.pin12
  N15: IC1.pin2, IC2.pin11
  N16: IC1.pin3, IC2.pin8
  N17: IC1.pin6, IC2.pin10
  N18: IC1.pin7, IC2.pin7
