# Fritzing sketch WorkTimeLoggerSchematic V2 (saved by Fritzing 0.9.3b)
breadboards: 1

parts:
  IC1 = IC, SIP package, 8 pins [chip_label=RC522]
  HD44780 = IC, SIP package, 4 pins [chip_label=PCF8574]
  OK = Pushbutton [package="[THT]"]
  ANULUJ = Pushbutton [package="[THT]"]
  IC2 = IC, DIP package, 12 pins [chip_label=LLC]
  U1 = atmega328 [package=dip]
  5V = Power plug
  3V3 = Power plug

nets:
  N1: IC1.pin1, IC2.pin12
  N2: IC1.pin2, IC2.pin11
  N3: IC1.pin3, IC2.pin8
  N4: IC1.pin4, U1.D12
  N5: IC1.pin5, U1.D2
  N6: IC1.pin6, IC2.pin10
  N7: IC1.pin7, IC2.pin7
  N8: IC1.pin8, IC2.pin9, 3V3.VCC
  N9: HD44780.pin1, U1.A5
  N10: HD44780.pin2, U1.A4
  VCC: HD44780.pin3, IC2.pin4, U1.VCC, U1.AVCC, 5V.VCC
  GND: HD44780.pin4, OK.Pin_1, OK.Pin_2, ANULUJ.Pin_1, ANULUJ.Pin_2, IC2.pin3, U1.GND, 5V.GND, 3V3.GND
  N11: OK.Pin_3, OK.Pin_4, U1.D4
  N12: ANULUJ.Pin_3, ANULUJ.Pin_4, U1.D3_(PWM)
  N13: IC2.pin1, U1.D10_(PWM)
  N14: IC2.pin2, U1.D13
  N15: IC2.pin5, U1.D11_(PWM)
  N16: IC2.pin6, U1.D9_(PWM)
